# Fritzing sketch MAIN_SKETCH (saved by Fritzing 0.9.3b)
breadboards: 1

parts:
  LCD1 = LCD screen
  IC1 = L293D [package=THT]
  Part2 = KY-001 Temperature Sensor Module [package="Breakout board"]
  DI1 = 7-Segment LED Display [package=THT]
  LCM1602_IIC1 = LCM1602 IIC [part_number="LCM1602 IIC" chip_label="LCM1602 IIC" package="DIP (Dual Inline) [THT]"]
  VCC1 = Battery block 9V
  M2 = DC Motor
  M3 = DC Motor
  Part3 = Arduino Uno (Rev3)
  U1 = SN74LS14N [package="DIP14 [THT]"]
  S1 = Taiway 100-SP-X-T1 SPDT Miniature Toggle Switch [part_number=100-SP-X-T1-0-0-B1-M2 package=THT]  # not connected

nets:
  GND: LCD1.VSS, IC1.0V, Part2.-, LCM1602_IIC1.VSS, LCM1602_IIC1.GND, LCM1602_IIC1.SCL, VCC1.-, Part3.A5/SCL, Part3.GND, U1.GND
  VDD: LCD1.VDD, LCM1602_IIC1.VDD
  N1: LCD1.V0, LCM1602_IIC1.V0
  N2: LCD1.RS, LCM1602_IIC1.RS
  N3: LCD1.R/W, LCM1602_IIC1.RW
  N4: LCD1.E, LCM1602_IIC1.E
  N5: LCD1.DB0, LCM1602_IIC1.D0
  N6: LCD1.DB1, LCM1602_IIC1.D1
  N7: LCD1.DB2, LCM1602_IIC1.D2
  N8: LCD1.DB3, LCM1602_IIC1.D3
  N9: LCD1.DB4, LCM1602_IIC1.D4
  N10: LCD1.DB5, LCM1602_IIC1.D5
  N11: LCD1.DB6, LCM1602_IIC1.D6
  N12: LCD1.DB7, LCM1602_IIC1.D7
  N13: LCD1.LED+, LCM1602_IIC1.A
  N14: LCD1.LED-, LCM1602_IIC1.K
  N15: IC1.Enable_1, Part3.D10_PWM/SS
  N16: IC1.In_1, Part3.D9_PWM
  N17: IC1.Out_1_(_Controlled_by_Enable_1_), M2.pin_1
  N18: IC1.Out_2_(_Controlled_by_Enable_1_), M2.pin_2
  N19: IC1.In_2, Part3.D8
  VIN: IC1.+Vmotor, IC1.+V, Part2.Vin, DI1.commAnode, LCM1602_IIC1.VCC, VCC1.+, Part3.5V, Part3.VIN, U1.1A, U1.VCC
  N20: IC1.Enable_2, Part3.D11_PWM/MOSI
  N21: IC1.In_3, Part3.D13/SCK
  N22: IC1.Out_3_(_Controlled_by_Enable_2_), M3.pin_2
  N23: IC1.Out_4_(_Controlled_by_Enable_2_), M3.pin_1
  N24: IC1.In_4, Part3.D12/MISO
  N25: Part2.S, Part3.D2
  N26: DI1.cathodeE, U1.5Y
  N27: DI1.cathodeD, U1.3Y
  N28: DI1.cathodeC, U1.5A
  N29: DI1.cathodeDP, U1.6A
  N30: DI1.cathodeB, U1.6Y
  N31: DI1.cathodeA, U1.2Y
  N32: DI1.cathodeF, U1.3A
  N33: DI1.cathodeG, U1.2A
  N34: LCM1602_IIC1.SDA, Part3.A4/SDA
  N35: Part3.D3_PWM, U1.1Y
  N36: Part3.D4, U1.4Y

custom parts:
  KY-001 Temperature Sensor Module: Arduino Temperature Sensor Module Keyes KY-001, Allows ambient temperature measurement using digital serial bus (DS18B20)
  LCM1602 IIC: I2C-Module to use a 1602 or 2004 LCD on with the wire.h libory Serial LCD Modul
